# Fritzing sketch PiBot_v4_wiring (saved by Fritzing 0.9.3b)
perfboards: 1

parts:
  MCU1 = Raspberry Pi Zero
  M1 = RioRand LM2596
  DRV_1 = DRV 8825 Stepper Motor Carrier, High Current [part_number="DRV 8825"]
  DRV_2 = DRV 8825 Stepper Motor Carrier, High Current [part_number="DRV 8825"]
  SM1 = 28BYJ-48 Stepper Motor [part_number=28BYJ-48]
  Driver1 = 28BYJ-48 Driver Module [part_number=ULN2003 package=THT]
  M2 = Stepper Motor - Bipolar  # not connected
  M3 = Stepper Motor - Bipolar  # not connected
  VCC1 = Battery block 9V  # not connected
  S1 = SPST Switch [package=switch-spdt-smd]
  S2 = SPST Switch [package=switch-spdt-smd]
  C1 = Electrolytic Capacitor [capacitance=1000μF package="1010 [SMD, electrolytic]"]  # not connected

nets:
  N1: MCU1.pin_1, MCU1.pin_17, DRV_1.RESET
  N2: MCU1.pin_2, MCU1.pin_4, Driver1.Vmotor
  N3: MCU1.pin_9, MCU1.pin_25, MCU1.pin_39, Driver1.GND
  N4: MCU1.pin_11, DRV_1.STEP
  N5: MCU1.pin_16, S1.O
  N6: MCU1.pin_18, DRV_2.SLEEP
  N7: MCU1.pin_36, Driver1.IN3
  N8: MCU1.pin_37, Driver1.IN4
  N9: MCU1.pin_38, Driver1.IN2
  N10: MCU1.pin_40, Driver1.IN1
  N11: M1.Pin_1, S2.P
  N12: SM1.blue-pin, Driver1.blue-pin
  N13: SM1.pink-pin, Driver1.pink-pin
  N14: SM1.yellow-pin, Driver1.yellow-pin
  N15: SM1.orange-pin, Driver1.orange-pin
  N16: SM1.red-pin, Driver1.red-pin

custom parts:
  28BYJ-48 Stepper Motor: Unipolar Stepper Motor 28BYJ-48 Top coil - pink & orange Bottom coil - blue & yellow Common rail - red Connector pins: blue - pink - yellow - orange - red
  28BYJ-48 Driver Module: ULN2003 Driver Module for the 28BYJ-48 Unipolar Stepper Motor LED A - Blue wire - Bottom coil left LED B - Pink wire - Top coil left LED C - Yellow wire - Bottom coil right LED D - Orange wire - Top coil right Common rail - red Connector pins: blue - pink - yellow - orange - red Control pins - IN1 to IN4 Power pins - GND & Vmotor (5-12V) On/Off jumper (if removed, power to motor is cut).
